# Fritzing sketch Word (saved by Fritzing 1.0.3b)

parts:
  Part1 = BH1750
  ZS-042_RTC1 = ZS-042 RTC Module
  U1 = WS2812 RGB LED strip
  Mod1 = Amica NodeMCU DEVKIT 1.0
  R1 = Photocell (LDR) [power=0.25W dark_resistance_@0.01lx=300kΩ light_resistance_@100lx=400Ω luminance=10lx package=THT]
  R2 = Resistor [tolerance=±5% power=0.25W resistance=220 package=THT]

nets:
  VCC: Part1.VCC, ZS-042_RTC1.VCC, Mod1.pin1, Mod1.pin_10, Mod1.pin_26, R1.pin_0
  GND: Part1.GND, ZS-042_RTC1.GND, U1.GND, Mod1.pin2, Mod1.pin_9, Mod1.pin_25, Mod1.pin_29, R2.Pin_1
  N1: Part1.SCL, Mod1.pin_12
  N2: Part1.SDA, Mod1.pin_11
  N3: ZS-042_RTC1.SDA, Mod1.pin_13
  N4: ZS-042_RTC1.SCL, Mod1.pin_14
  N5: U1.VCC, Mod1.pin_30
  N6: U1.DIN, Mod1.pin4
  N7: Mod1.pin_16, R1.pin_1, R2.Pin_0

notes:
  DS3231
  (RTC)
  (Optional)
  BH1750
  (Lux Sensor)
  (optional)
  LED Stripe (WS2812b or SK26812)
  ESP8266
  LDR
  (optional)

custom parts:
  BH1750: Light Sensor
  WS2812 RGB LED strip: WS2812 strip
